// Logisim project conversor BCD 7 SEGMENTOS.circ as structural Verilog
module conversor_bcd (
  input  A,
  input  B,
  input  C,
  input  D
);

  wire and_1_out, and_2_out, and_3_out, and_4_out, and_5_out, and_6_out, and_7_out, not_1_out, or_1_out,
       or_2_out, or_3_out, or_4_out, or_5_out, or_6_out, or_7_out, or_8_out, or_9_out, or_10_out, or_11_out,
       or_12_out, or_13_out, xor_1_out, xor_2_out, xor_3_out;

  xor xor_1 (xor_1_out, B, D);
  xor xor_2 (xor_2_out, C, D);
  or or_1 (or_1_out, B, ~C, D);  // OR_Gate
  or or_2 (or_2_out, C, ~D);  // OR_Gate
  xor xor_3 (xor_3_out, B, C);
  and and_1 (and_1_out, C, ~D);  // AND_Gate
  or or_3 (or_3_out, A, C);
  or or_4 (or_4_out, or_3_out, not_1_out);
  not not_1 (not_1_out, xor_1_out);
  or or_5 (or_5_out, ~B, ~xor_2_out);  // OR_Gate
  or or_6 (or_6_out, A, and_2_out);
  and and_2 (and_2_out, or_2_out, ~B);  // AND_Gate
  and and_3 (and_3_out, B, ~C, D);  // AND_Gate
  and and_4 (and_4_out, C, ~D);  // AND_Gate
  or or_7 (or_7_out, C, ~B);  // OR_Gate
  and and_5 (and_5_out, or_7_out, ~D);  // AND_Gate
  or or_8 (or_8_out, A, B);
  and and_6 (and_6_out, or_8_out, or_9_out);
  or or_9 (or_9_out, ~C, ~D);  // OR_Gate
  and and_7 (and_7_out, ~C, ~D);  // AND_Gate
  or or_10 (or_10_out, A, xor_3_out, and_1_out);
  or or_11 (or_11_out, or_6_out, and_3_out);
  or or_12 (or_12_out, and_6_out, and_7_out);
  or or_13 (or_13_out, or_11_out, and_4_out);
  _7_Segment_Display u_7_segment_display_1 (
    .g(or_10_out), .f(or_12_out), .a(or_4_out), .b(or_5_out), .e(and_5_out), .d(or_13_out), .c(or_1_out));  // open: dp
endmodule

// L1
module conversor_l7 (
  input  A,
  input  B,
  input  C,
  output out_4,
  output out_5,
  output out_6,
  output out_7,
  output out_8,
  output out_9,
  output out_10
);

  wire and_1_out, and_2_out, and_3_out;

  and and_1 (and_1_out, B, C);
  and and_2 (and_2_out, A, C);
  and and_3 (and_3_out, A, B);
  and and_4 (out_9, A, B);
  and and_5 (out_10, A, B, C);
  or or_1 (out_4, A, B, C);
  or or_2 (out_5, A, B);
  or or_3 (out_6, and_1_out, A);
  or or_4 (out_8, and_2_out, and_3_out);

  assign out_7 = A;
endmodule
